# Fritzing sketch wiring (saved by Fritzing 0.9.3b)
breadboards: 1

parts:
  microSD1 = MicroSD Card Module
  Part1 = Arduino Due (Rev2b)
  ZS-042_RTC1 = ZS-042 RTC Module
  Part2 = RFID-RC522
  Part3 = sensor_biometrico
  R1 = Resistor [tolerance=±5% resistance=33 package=THT]
  R2 = Resistor [tolerance=±5% resistance=3k package=THT]

nets:
  N1: microSD1.GND, Part1.D12_PWM, R2.Pin_0
  VCC: microSD1.VCC, Part1.IOREF, ZS-042_RTC1.VCC, Part2.3_3V, Part3.VCC
  N2: microSD1.MISO, R1.Pin_1
  N3: microSD1.MOSI, Part2.MOSI
  N4: microSD1.SCK, Part2.SCK
  N5: microSD1.CS, Part1.D10_PWM/SS0
  N6: Part1.D14/TX3, Part3.TX
  N7: Part1.D15/RX3, Part3.RX
  N8: Part1.D20/SDA3, ZS-042_RTC1.SDA
  N9: Part1.D21/SCL3, ZS-042_RTC1.SCL
  GND: Part1.GND, ZS-042_RTC1.GND, Part2.GND, Part3.GND, R2.Pin_1
  N10: Part1.D8_PWM, Part2.SDA
  N11: Part1.D9_PWM, Part2.RST
  N12: Part2.MISO, R1.Pin_0

custom parts:
  RFID-RC522: The simple China made RFID reader
  sensor_biometrico: Adafruit Optical Fingerprint Sensor
